# Fritzing sketch Plant Shelf (saved by Fritzing 0.9.2b)
breadboards: 1

parts:
  Part1 = Photon
  Q1 = NPN-Transistor [package="TO92 [THT]"]
  V1 = DC Power [voltage=5]
  Part2 = FC-28 Soil Hygrometer Module
  Part3 = FC-28 Soil Hygrometer Module
  Part4 = FC-28 Soil Hygrometer Module
  Part5 = FC-28 Soil Hygrometer Module
  Q2 = NPN-Transistor [package="TO92 [THT]"]
  Q3 = NPN-Transistor [package="TO92 [THT]"]
  R2 = Resistor [tolerance=±5% resistance=1.5k package=THT]
  R3 = Resistor [tolerance=±5% resistance=1.5k package=THT]
  U1 = RELAY [package=relay-t9a-2]
  U2 = RELAY [package=relay-t9a-2]
  U3 = TMP36 [package=to-92]
  R4 = Resistor [tolerance=±5% resistance=4.7k package="0805 [SMD]"]
  U4 = LCD-16X2 [package=lcd-16x2]  # not connected
  Part6 = Adafruit I2C+SPI LCD Backpack [part_number="Adafruit #292"]  # not connected
  R1 = Resistor [tolerance=±5% resistance=1.5k package="2010 [SMD]"]

nets:
  N1: Part1.A0, Part2.AO
  N2: Part1.A1, Part3.AO
  N3: Part1.A2, Part4.AO
  N4: Part1.A3, Part5.AO
  N5: Part1.A4, U3.VOUT, R4.Pin_1
  GND: Part1.GND, V1.V-, Part2.GND, Part3.GND, Part4.GND, Part5.GND, R2.Pin_0, R3.Pin_0, U1.COIL2, U2.COIL2, U3.GND, R1.Pin_0
  N6: Part1.D4, Q1.B
  N7: Part1.D5, Q2.B
  N8: Part1.D6, Q3.B
  3V3: Part1.3V3, U3.VCC, R4.Pin_0
  VCC: Q1.E, Part2.VCC, Part3.VCC, Part4.VCC, Part5.VCC, R1.Pin_1
  N9: Q1.C, V1.V+, Q2.C, Q3.C
  N10: Q2.E, R2.Pin_1, U2.COIL1
  N11: Q3.E, R3.Pin_1, U1.COIL1

custom parts:
  FC-28 Soil Hygrometer Module: The FC-28 is a soil hygrometer module that uses the Texas Instruments LM393 comparator chip to provide an analog measurement of soil humidity. The digital output is high when soil moisture is over a certain threshold, as determined by adjusting the potentiometer.
  Adafruit I2C+SPI LCD Backpack: LCD backpacks reduce the number of pins needed to connect to an LCD. LCDs are a fun and easy way to have your microcontroller project talk back to you. Character LCDs are common, and easy to get, available in tons of colors and sizes. We've written tutorials on using character LCDs with an Arduino (or similar microcontroller) but find that the number of pins necessary to control the LCD can be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
